# Fritzing sketch Configuración Bluetooth HC-05 (saved by Fritzing 0.9.3b)

parts:
  Componente1 = Arduino Nano (Rev3.0)
  Componente2 = Bluetooth HC-05 Macho

nets:
  GND: Componente1.GND, Componente2.GND
  N1: Componente1.D9, Componente2.RXD
  N2: Componente1.D10, Componente2.TXD
  5V: Componente1.5V, Componente2.VCC
